// Digital circuit mico.dig as structural Verilog
module mico (
  input  clk,
  output out_1,
  output [31:0] display
);

  wire comparator_1_eq;
  wire [10:0] rom_2_d;
  wire [15:0] add_1_s, multiplexer_1_out, multiplexer_2_out, multiplexer_3_out, register_1_q;
  wire [31:0] bitextender_1_out, bitextender_2_out, multiplexer_4_out, multiplexer_5_out, ramdualport_1_d,
       registrador_1_b_2, rom_1_d, ula_1_y;

  Multiplexer #(.Bits(16)) multiplexer_1 (
    .sel(rom_2_d[10]), .in_0(multiplexer_2_out), .in_1(register_1_q), .out(multiplexer_1_out));
  Add #(.Bits(16)) add_1 (.a(16'h1), .b(register_1_q), .c_i(1'b0), .s(add_1_s));  // open: c_o
  Multiplexer #(.Selector_Bits(2), .Bits(16)) multiplexer_2 (
    .sel(rom_2_d[8:7]), .in_0(add_1_s), .in_1(rom_1_d[15:0]), .in_2(display[15:0]), .in_3(multiplexer_3_out),
    .out(multiplexer_2_out));
  Register #(.Bits(16)) register_1 (.D(multiplexer_1_out), .C(clk), .en(1'b1), .Q(register_1_q));
  ROM #(.AddrBits(16), .Bits(32)) rom_1 (.A(register_1_q), .sel(1'b1), .D(rom_1_d));
  BitExtender #(.inputBits(16), .outputBits(32)) bitextender_1 (.in(multiplexer_1_out), .out(bitextender_1_out));
  Multiplexer #(.Bits(16)) multiplexer_3 (
    .sel(comparator_1_eq), .in_0(register_1_q), .in_1(rom_1_d[15:0]), .out(multiplexer_3_out));
  registrador registrador_1 (
    .C(multiplexer_5_out), .a(rom_1_d[27:24]), .b(rom_1_d[23:20]), .c_2(rom_1_d[19:16]), .wr(rom_2_d[9]),
    .clock(clk), .A_2(display), .B_2(registrador_1_b_2));
  BitExtender #(.inputBits(16), .outputBits(32)) bitextender_2 (.in(rom_1_d[15:0]), .out(bitextender_2_out));
  Multiplexer #(.Bits(32)) multiplexer_4 (
    .sel(rom_2_d[2]), .in_0(registrador_1_b_2), .in_1(bitextender_2_out), .out(multiplexer_4_out));
  ROM #(.AddrBits(4), .Bits(11)) rom_2 (.A(rom_1_d[31:28]), .sel(1'b1), .D(rom_2_d));
  Comparator #(.Bits(32)) comparator_1 (.a(display), .b(registrador_1_b_2), .eq(comparator_1_eq));  // open: gt, lt
  ula ula_1 (.a(multiplexer_4_out), .b(display), .fun(rom_2_d[5:3]), .overflow(out_1), .y(ula_1_y));
  Multiplexer #(.Selector_Bits(2), .Bits(32)) multiplexer_5 (
    .sel(rom_2_d[1:0]), .in_0(ula_1_y), .in_1(ramdualport_1_d), .in_2(bitextender_1_out), .in_3({32{1'b0}}),
    .out(multiplexer_5_out));
  RAMDualPort #(.AddrBits(16), .Bits(32)) ramdualport_1 (
    .A(ula_1_y[15:0]), .Din(registrador_1_b_2), .str(rom_2_d[6]), .C(clk), .ld(1'b1), .D(ramdualport_1_d));

  // Notes on the sheet:
  //   halt
  //   const
  //   contents of rom_2 (hex, n*v repeats v):
  //   200,208,210,218,220,228,230,238,204,205,44,283,102,600,380,400
  //   2 selC
  //   1 selB
  //   3 ulafun
  //   1 ram
  //   2 ip
  //   1 wr
  //   1halt
endmodule
