// Digital circuit ula.dig as structural Verilog
module ula (
  input  [31:0] a,
  input  [31:0] b,
  input  [2:0] fun,
  output overflow,
  output [31:0] y
);

  wire add_1_c_o, comparator_1_lt, decoder_1_out_1;
  wire [31:0] add_1_s, and_1_out, multiplexer_1_out, multiplexer_2_out, not_1_out, not_2_out, or_1_out,
       xor_1_out;
  wire [63:0] mul_1_mul;

  assign not_1_out = ~b;  // Not not_1, 32 bits wide
  Multiplexer #(.Bits(32)) multiplexer_1 (.sel(decoder_1_out_1), .in_0(b), .in_1(not_1_out), .out(multiplexer_1_out));
  Decoder #(.Selector_Bits(3)) decoder_1 (
    .sel(fun), .out_1(decoder_1_out_1));  // open: out_0, out_2, out_3, out_4, out_5, out_6, out_7
  Add #(.Bits(32)) add_1 (.a(a), .b(multiplexer_1_out), .c_i(decoder_1_out_1), .s(add_1_s), .c_o(add_1_c_o));
  Mul #(.Bits(32)) mul_1 (.a(a), .b(multiplexer_1_out), .mul(mul_1_mul));
  assign and_1_out = a & multiplexer_1_out;  // And and_1, 32 bits wide
  assign or_1_out = a | multiplexer_1_out;  // Or or_1, 32 bits wide
  assign xor_1_out = a ^ multiplexer_1_out;  // XOr xor_1, 32 bits wide
  Comparator #(.Bits(32)) comparator_1 (.a(a), .b(multiplexer_1_out), .lt(comparator_1_lt));  // open: gt, eq
  assign not_2_out = ~a;  // Not not_2, 32 bits wide
  and and_2 (overflow, add_1_c_o, ~decoder_1_out_1);  // And
  Multiplexer #(.Bits(32)) multiplexer_2 (
    .sel(comparator_1_lt), .in_0({32{1'b0}}), .in_1(32'h1), .out(multiplexer_2_out));
  Multiplexer #(.Selector_Bits(3), .Bits(32)) multiplexer_3 (
    .sel(fun), .in_0(add_1_s), .in_1(add_1_s), .in_2(mul_1_mul[31:0]), .in_3(and_1_out), .in_4(or_1_out),
    .in_5(xor_1_out), .in_6(multiplexer_2_out), .in_7(not_2_out), .out(y));
endmodule
